# Fritzing sketch rocket (saved by Fritzing 0.9.6b)
breadboards: 1

parts:
  Part1 = Arduino Nano (Rev3.0)
  Mod1 = ossoyoo-lora-module
  VCC1 = Battery block 9V
  U1 = Voltage Regulator [package=to220-igo]

nets:
  N1: Part1.D1/TX, Mod1.TXD
  N2: Part1.D0/RX, Mod1.RXD
  GND: Part1.GND, Mod1.M0, Mod1.M1, Mod1.GND, VCC1.-, U1.GND
  N3: Part1.VIN, VCC1.+, U1.IN
  N4: Mod1.VCC, U1.OUT

custom parts:
  ossoyoo-lora-module: Osoyoo Long Distance wireless transceiver Uart LoRa Module.
